# Fritzing sketch OpenROV-mcu (saved by Fritzing 0.7.4b)
breadboards: 1

parts:
  XTAL1 = Crystal [frequency="16 Mhz" package=THT]
  C1 = Ceramic Capacitor [capacitance=22pF package="100 mil [THT, multilayer]"]
  C2 = Ceramic Capacitor [capacitance=22pF package="100 mil [THT, multilayer]"]
  U1 = atmega328 [package=dip]

nets:
  N1: XTAL1.pin_0, C2.1, U1.XLAT1
  N2: XTAL1.pin_1, C1.1, U1.XLAT2
  GND: C1.0, C2.0, U1.GND
  5V: U1.VCC, U1.AVCC, U1.AREF
